# Fritzing sketch mk (saved by Fritzing 0.9.3b)
perfboards: 4

parts:
  Row_1_-_Red = Packages: [package=dil28-3]
  Row_1_-_Green = Packages: [package=dil28-3]
  Row_1_-_Blue = Packages: [package=dil28-3]
  Row_3_-_Green = Packages: [package=dil28-3]  # not connected
  Row_4_-_Green = Packages: [package=dil28-3]  # not connected
  Row_2_-_Red = Packages: [package=dil28-3]
  Row_2_-_Green = Packages: [package=dil28-3]
  Row_2_-_Blue = Packages: [package=dil28-3]
  Row_3_-_Blue = Packages: [package=dil28-3]  # not connected
  Row_4_-_Blue = Packages: [package=dil28-3]  # not connected
  Row_4_-_Red = Packages: [package=dil28-3]  # not connected
  Row_3_-_Red = Packages: [package=dil28-3]  # not connected
  LED9 = RGB LED (com. anode, rbg) [package="5 mm [THT]"]  # not connected
  LED10 = RGB LED (com. anode, rbg) [package="5 mm [THT]"]
  LED44 = RGB LED (com. anode, rbg) [package="5 mm [THT]"]  # not connected
  LED46 = RGB LED (com. anode, rbg) [package="5 mm [THT]"]  # not connected
  LED48 = RGB LED (com. anode, rbg) [package="5 mm [THT]"]  # not connected
  LED49 = RGB LED (com. anode, rbg) [package="5 mm [THT]"]  # not connected
  LED50 = RGB LED (com. anode, rbg) [package="5 mm [THT]"]  # not connected
  LED51 = RGB LED (com. anode, rbg) [package="5 mm [THT]"]  # not connected
  LED52 = RGB LED (com. anode, rbg) [package="5 mm [THT]"]  # not connected
  LED53 = RGB LED (com. anode, rbg) [package="5 mm [THT]"]  # not connected
  LED54 = RGB LED (com. anode, rbg) [package="5 mm [THT]"]  # not connected
  LED55 = RGB LED (com. anode, rbg) [package="5 mm [THT]"]  # not connected
  LED1 = RGB LED (com. anode, rbg) [package="5 mm [THT]"]
  J34 = double row female pin header, 16 pins [form="♀ (female)"]  # not connected
  J63 = double row female pin header, 16 pins [form="♀ (female)"]  # not connected
  J64 = double row female pin header, 16 pins [form="♀ (female)"]  # not connected
  J65 = double row female pin header, 16 pins [form="♀ (female)"]  # not connected
  J66 = double row female pin header, 16 pins [form="♀ (female)"]
  J67 = double row female pin header, 16 pins [form="♀ (female)"]
  J68 = double row female pin header, 16 pins [form="♀ (female)"]
  J69 = double row female pin header, 16 pins [form="♀ (female)"]
  J70 = double row female pin header, 16 pins [form="♀ (female)"]
  J71 = double row female pin header, 16 pins [form="♀ (female)"]
  J72 = double row female pin header, 16 pins [form="♀ (female)"]
  J73 = double row female pin header, 16 pins [form="♀ (female)"]
  J74 = double row female pin header, 16 pins [form="♀ (female)"]  # not connected
  J75 = double row female pin header, 16 pins [form="♀ (female)"]  # not connected
  J76 = double row female pin header, 16 pins [form="♀ (female)"]  # not connected
  J77 = double row female pin header, 16 pins [form="♀ (female)"]  # not connected
  J80 = female pin header, 10 pins [form="♀ (female)"]
  J81 = female pin header, 10 pins [form="♀ (female)"]
  Teensy_3_1 = Teensy 3.1
  R3 = Resistor [tolerance=±5% resistance=2.2k package=THT]
  J83 = female pin header, 14 pins [form="♀ (female)"]  # not connected
  J84 = female pin header, 14 pins [form="♀ (female)"]  # not connected
  J85 = female pin header, 5 pins [form="♀ (female)"]  # not connected
  R7 = Resistor [tolerance=±5% resistance=2.2k package=THT]
  R9 = Resistor [tolerance=±5% resistance=2.2k package=THT]
  R11 = Resistor [tolerance=±5% resistance=10k package=THT]
  R12 = Resistor [tolerance=±5% resistance=2.2k package=THT]
  R13 = Resistor [tolerance=±5% resistance=10k package=THT]
  R14 = Resistor [tolerance=±5% resistance=2.2k package=THT]
  R15 = Resistor [tolerance=±5% resistance=2.2k package=THT]
  R16 = Resistor [tolerance=±5% resistance=10k package=THT]
  LED67 = RGB LED (com. anode, rbg) [package="5 mm [THT]"]
  LED68 = RGB LED (com. anode, rbg) [package="5 mm [THT]"]
  LED69 = RGB LED (com. anode, rbg) [package="5 mm [THT]"]  # not connected
  LED70 = RGB LED (com. anode, rbg) [package="5 mm [THT]"]  # not connected
  LED71 = RGB LED (com. anode, rbg) [package="5 mm [THT]"]  # not connected
  LED72 = RGB LED (com. anode, rbg) [package="5 mm [THT]"]  # not connected
  LED73 = RGB LED (com. anode, rbg) [package="5 mm [THT]"]  # not connected
  LED74 = RGB LED (com. anode, rbg) [package="5 mm [THT]"]  # not connected
  LED75 = RGB LED (com. anode, rbg) [package="5 mm [THT]"]  # not connected
  LED76 = RGB LED (com. anode, rbg) [package="5 mm [THT]"]  # not connected
  LED77 = RGB LED (com. anode, rbg) [package="5 mm [THT]"]  # not connected
  LED78 = RGB LED (com. anode, rbg) [package="5 mm [THT]"]  # not connected
  LED79 = RGB LED (com. anode, rbg) [package="5 mm [THT]"]  # not connected
  R10 = Resistor [tolerance=±5% resistance=10k package=THT]
  R8 = Resistor [tolerance=±5% resistance=10k package=THT]
  R2 = Resistor [tolerance=±5% resistance=10k package=THT]
  S5 = SWITCH-MOMENTARY-2 [package=tactile-pth]
  S4 = SWITCH-MOMENTARY-2 [package=tactile-pth]
  S6 = SWITCH-MOMENTARY-2 [package=tactile-pth]
  S7 = SWITCH-MOMENTARY-2 [package=tactile-pth]
  S8 = SWITCH-MOMENTARY-2 [package=tactile-pth]
  S9 = SWITCH-MOMENTARY-2 [package=tactile-pth]
  S10 = SWITCH-MOMENTARY-2 [package=tactile-pth]
  S11 = SWITCH-MOMENTARY-2 [package=tactile-pth]
  S12 = SWITCH-MOMENTARY-2 [package=tactile-pth]
  S13 = SWITCH-MOMENTARY-2 [package=tactile-pth]
  S14 = SWITCH-MOMENTARY-2 [package=tactile-pth]
  S15 = SWITCH-MOMENTARY-2 [package=tactile-pth]
  S16 = SWITCH-MOMENTARY-2 [package=tactile-pth]
  S17 = SWITCH-MOMENTARY-2 [package=tactile-pth]
  S18 = SWITCH-MOMENTARY-2 [package=tactile-pth]
  S19 = SWITCH-MOMENTARY-2 [package=tactile-pth]
  S20 = SWITCH-MOMENTARY-2 [package=tactile-pth]
  S21 = SWITCH-MOMENTARY-2 [package=tactile-pth]
  S22 = SWITCH-MOMENTARY-2 [package=tactile-pth]
  S23 = SWITCH-MOMENTARY-2 [package=tactile-pth]
  S24 = SWITCH-MOMENTARY-2 [package=tactile-pth]
  S25 = SWITCH-MOMENTARY-2 [package=tactile-pth]
  S26 = SWITCH-MOMENTARY-2 [package=tactile-pth]
  S27 = SWITCH-MOMENTARY-2 [package=tactile-pth]
  S28 = SWITCH-MOMENTARY-2 [package=tactile-pth]
  S29 = SWITCH-MOMENTARY-2 [package=tactile-pth]
  S30 = SWITCH-MOMENTARY-2 [package=tactile-pth]
  S31 = SWITCH-MOMENTARY-2 [package=tactile-pth]
  S32 = SWITCH-MOMENTARY-2 [package=tactile-pth]
  S33 = SWITCH-MOMENTARY-2 [package=tactile-pth]
  S34 = SWITCH-MOMENTARY-2 [package=tactile-pth]
  S35 = SWITCH-MOMENTARY-2 [package=tactile-pth]
  S36 = SWITCH-MOMENTARY-2 [package=tactile-pth]
  S37 = SWITCH-MOMENTARY-2 [package=tactile-pth]
  S38 = SWITCH-MOMENTARY-2 [package=tactile-pth]
  S39 = SWITCH-MOMENTARY-2 [package=tactile-pth]
  S40 = SWITCH-MOMENTARY-2 [package=tactile-pth]
  S41 = SWITCH-MOMENTARY-2 [package=tactile-pth]
  S42 = SWITCH-MOMENTARY-2 [package=tactile-pth]
  S43 = SWITCH-MOMENTARY-2 [package=tactile-pth]
  S44 = SWITCH-MOMENTARY-2 [package=tactile-pth]
  S45 = SWITCH-MOMENTARY-2 [package=tactile-pth]
  S46 = SWITCH-MOMENTARY-2 [package=tactile-pth]
  S47 = SWITCH-MOMENTARY-2 [package=tactile-pth]
  S48 = SWITCH-MOMENTARY-2 [package=tactile-pth]
  S50 = SWITCH-MOMENTARY-2 [package=tactile-pth]
  S51 = SWITCH-MOMENTARY-2 [package=tactile-pth]
  S52 = SWITCH-MOMENTARY-2 [package=tactile-pth]
  S53 = SWITCH-MOMENTARY-2 [package=tactile-pth]
  S54 = SWITCH-MOMENTARY-2 [package=tactile-pth]
  S55 = SWITCH-MOMENTARY-2 [package=tactile-pth]
  D1 = Diode [package=diode-1n4148]
  D2 = Diode [package=diode-1n4148]
  D3 = Diode [package=diode-1n4148]
  D4 = Diode [package=diode-1n4148]
  D5 = Diode [package=diode-1n4148]
  D6 = Diode [package=diode-1n4148]
  D7 = Diode [package=diode-1n4148]
  D8 = Diode [package=diode-1n4148]
  D9 = Diode [package=diode-1n4148]
  D10 = Diode [package=diode-1n4148]
  D11 = Diode [package=diode-1n4148]
  D12 = Diode [package=diode-1n4148]
  D13 = Diode [package=diode-1n4148]
  D14 = Diode [package=diode-1n4148]
  D15 = Diode [package=diode-1n4148]
  D16 = Diode [package=diode-1n4148]
  D17 = Diode [package=diode-1n4148]
  D18 = Diode [package=diode-1n4148]
  D19 = Diode [package=diode-1n4148]
  D20 = Diode [package=diode-1n4148]
  D21 = Diode [package=diode-1n4148]
  D22 = Diode [package=diode-1n4148]
  D23 = Diode [package=diode-1n4148]
  D24 = Diode [package=diode-1n4148]
  D25 = Diode [package=diode-1n4148]
  D26 = Diode [package=diode-1n4148]
  D27 = Diode [package=diode-1n4148]
  D28 = Diode [package=diode-1n4148]
  D29 = Diode [package=diode-1n4148]
  D30 = Diode [package=diode-1n4148]
  D31 = Diode [package=diode-1n4148]
  D32 = Diode [package=diode-1n4148]
  D33 = Diode [package=diode-1n4148]
  D34 = Diode [package=diode-1n4148]
  D35 = Diode [package=diode-1n4148]
  D36 = Diode [package=diode-1n4148]
  D37 = Diode [package=diode-1n4148]
  D38 = Diode [package=diode-1n4148]
  D39 = Diode [package=diode-1n4148]
  D40 = Diode [package=diode-1n4148]
  D41 = Diode [package=diode-1n4148]
  D42 = Diode [package=diode-1n4148]
  D43 = Diode [package=diode-1n4148]
  D44 = Diode [package=diode-1n4148]
  D45 = Diode [package=diode-1n4148]
  D47 = Diode [package=diode-1n4148]
  D48 = Diode [package=diode-1n4148]
  D49 = Diode [package=diode-1n4148]
  D50 = Diode [package=diode-1n4148]
  D51 = Diode [package=diode-1n4148]
  D52 = Diode [package=diode-1n4148]
  LED80 = RGB LED (com. anode, rbg) [package="5 mm [THT]"]
  LED81 = RGB LED (com. anode, rbg) [package="5 mm [THT]"]
  LED82 = RGB LED (com. anode, rbg) [package="5 mm [THT]"]  # not connected
  LED83 = RGB LED (com. anode, rbg) [package="5 mm [THT]"]  # not connected
  LED84 = RGB LED (com. anode, rbg) [package="5 mm [THT]"]  # not connected
  LED85 = RGB LED (com. anode, rbg) [package="5 mm [THT]"]  # not connected
  LED86 = RGB LED (com. anode, rbg) [package="5 mm [THT]"]  # not connected
  LED87 = RGB LED (com. anode, rbg) [package="5 mm [THT]"]  # not connected
  J82 = female pin header, 8 pins [form="♀ (female)"]
  J86 = female pin header, 8 pins [form="♀ (female)"]
  J87 = female pin header, 8 pins [form="♀ (female)"]

nets:
  N1: Row_1_-_Red.OUT1, LED10.red_cathode, J67.pin15
  N2: Row_1_-_Red.SOUT, Row_1_-_Green.SIN
  N3: Row_1_-_Red.GSCLK, Row_1_-_Green.GSCLK, Row_1_-_Blue.GSCLK, Row_2_-_Red.GSCLK, Row_2_-_Green.GSCLK, Row_2_-_Blue.GSCLK, Teensy_3_1.D5, J82.pin1, J86.pin3, J87.pin3
  VCC: Row_1_-_Red.DCPRG, Row_1_-_Red.VCC, Row_1_-_Green.DCPRG, Row_1_-_Green.VCC, Row_1_-_Blue.DCPRG, Row_1_-_Blue.VCC, Row_2_-_Red.DCPRG, Row_2_-_Red.VCC, Row_2_-_Green.DCPRG, Row_2_-_Green.VCC, Row_2_-_Blue.DCPRG, Row_2_-_Blue.VCC, LED10.common_anode, LED1.common_anode, J66.pin1, J66.pin2, J66.pin3, J66.pin4, J66.pin5, J66.pin6, J66.pin7, J66.pin8, J66.pin9, J66.pin10, J66.pin11, J66.pin12, J66.pin13, J66.pin14, J66.pin15, J66.pin16, Teensy_3_1.3V3, R11.Pin_0, R13.Pin_0, R16.Pin_0, R10.Pin_0, R8.Pin_0, R2.Pin_1, LED80.common_anode, LED81.common_anode, J82.pin6, J86.pin6, J87.pin6
  N4: Row_1_-_Red.IREF, R3.Pin_0
  GND: Row_1_-_Red.GND, Row_1_-_Green.GND, Row_1_-_Blue.GND, Row_2_-_Red.GND, Row_2_-_Green.GND, Row_2_-_Blue.GND, J71.pin1, J71.pin2, J71.pin3, J71.pin4, J71.pin5, J71.pin6, J71.pin7, J71.pin8, J71.pin9, J71.pin10, J71.pin11, J71.pin12, J71.pin13, J71.pin14, J71.pin15, J71.pin16, Teensy_3_1.GND, R3.Pin_1, R7.Pin_0, R9.Pin_0, R12.Pin_0, R14.Pin_0, R15.Pin_0, LED67.common_anode, LED68.common_anode, J82.pin5, J86.pin5, J87.pin5
  N5: Row_1_-_Red.BLANK, Row_1_-_Green.BLANK, Row_1_-_Blue.BLANK, Row_2_-_Red.BLANK, Row_2_-_Green.BLANK, Row_2_-_Blue.BLANK, Teensy_3_1.D4, R11.Pin_1, R13.Pin_1, R16.Pin_1, R10.Pin_1, R8.Pin_1, R2.Pin_0, J82.pin3, J86.pin2, J87.pin2
  N6: Row_1_-_Red.XLAT, Row_1_-_Green.XLAT, Row_1_-_Blue.XLAT, Row_2_-_Red.XLAT, Row_2_-_Green.XLAT, Row_2_-_Blue.XLAT, Teensy_3_1.D3, J82.pin2, J86.pin1, J87.pin1
  N7: Row_1_-_Red.SCLK, Row_1_-_Green.SCLK, Row_1_-_Blue.SCLK, Row_2_-_Red.SCLK, Row_2_-_Green.SCLK, Row_2_-_Blue.SCLK, Teensy_3_1.D7, J82.pin4, J86.pin4, J87.pin4
  N8: Row_1_-_Red.SIN, Teensy_3_1.D1
  N9: Row_1_-_Red.VPRG, Row_1_-_Green.VPRG, Row_1_-_Blue.VPRG, Row_2_-_Red.VPRG, Row_2_-_Green.VPRG, Row_2_-_Blue.VPRG, Teensy_3_1.D2, J82.pin7, J86.pin7, J87.pin7
  N10: Row_1_-_Red.OUT0, LED1.red_cathode, J67.pin16
  N11: Row_1_-_Green.OUT1, LED10.green_cathode, J69.pin2
  N12: Row_1_-_Green.SOUT, Row_1_-_Blue.SIN
  N13: Row_1_-_Green.IREF, R7.Pin_1
  N14: Row_1_-_Green.OUT0, LED1.green_cathode, J69.pin1
  N15: Row_1_-_Blue.OUT1, LED10.blue_cathode, J68.pin2
  N16: Row_1_-_Blue.SOUT, Row_2_-_Red.SIN, J82.pin8, J86.pin8
  N17: Row_1_-_Blue.IREF, R9.Pin_1
  N18: Row_1_-_Blue.OUT0, LED1.blue_cathode, J68.pin1
  N19: Row_2_-_Red.OUT1, J73.pin2, LED68.red_cathode
  N20: Row_2_-_Red.SOUT, Row_2_-_Green.SIN
  N21: Row_2_-_Red.IREF, R15.Pin_1
  N22: Row_2_-_Red.OUT0, J73.pin1, LED67.red_cathode
  N23: Row_2_-_Green.OUT1, J72.pin2, LED68.green_cathode
  N24: Row_2_-_Green.SOUT, Row_2_-_Blue.SIN
  N25: Row_2_-_Green.IREF, R14.Pin_1
  N26: Row_2_-_Green.OUT0, J72.pin1, LED67.green_cathode
  N27: Row_2_-_Blue.OUT1, J70.pin2, LED68.blue_cathode
  N28: Row_2_-_Blue.SOUT, J87.pin8
  N29: Row_2_-_Blue.IREF, R12.Pin_1
  N30: Row_2_-_Blue.OUT0, J70.pin1, LED67.blue_cathode
  N31: J67.pin1, LED81.red_cathode
  N32: J67.pin2, LED80.red_cathode
  N33: J68.pin15, LED80.blue_cathode
  N34: J68.pin16, LED81.blue_cathode
  N35: J69.pin15, LED80.green_cathode
  N36: J69.pin16, LED81.green_cathode
  N37: J80.pin1, S4.1, S17.1, S30.1, S43.1
  N38: J80.pin2, S5.1, S18.1, S31.1, S44.1
  N39: J80.pin3, S6.1, S19.1, S32.1, S45.1
  N40: J80.pin4, S7.1, S20.1, S33.1, S46.1
  N41: J80.pin5, S8.1, S21.1, S34.1, S47.1
  N42: J80.pin6, S9.1, S22.1, S35.1, S48.1
  N43: J80.pin7, S10.1, S23.1, S36.1
  N44: J80.pin8, S11.1, S24.1, S37.1, S50.1
  N45: J80.pin9, S12.1, S25.1, S38.1, S51.1
  N46: J80.pin10, S13.1, S26.1, S39.1, S52.1
  N47: J81.pin1, S14.1, S27.1, S40.1, S53.1
  N48: J81.pin2, S15.1, S28.1, S41.1, S54.1
  N49: J81.pin3, S16.1, S29.1, S42.1, S55.1
  N50: J81.pin4, D1.C, D2.C, D3.C, D4.C, D5.C, D6.C, D7.C, D8.C, D9.C, D10.C, D11.C, D12.C, D13.C
  N51: J81.pin5, D14.C, D15.C, D16.C, D17.C, D18.C, D19.C, D20.C, D21.C, D22.C, D23.C, D24.C, D25.C, D26.C
  N52: J81.pin6, D27.C, D28.C, D29.C, D30.C, D31.C, D32.C, D33.C, D34.C, D35.C, D36.C, D37.C, D38.C, D39.C
  N53: J81.pin7, D40.C, D41.C, D42.C, D43.C, D44.C, D45.C, D47.C, D48.C, D49.C, D50.C, D51.C, D52.C
  N54: S5.2, D2.A
  N55: S4.2, D1.A
  N56: S6.2, D3.A
  N57: S7.2, D4.A
  N58: S8.2, D5.A
  N59: S9.2, D6.A
  N60: S10.2, D7.A
  N61: S11.2, D8.A
  N62: S12.2, D9.A
  N63: S13.2, D10.A
  N64: S14.2, D11.A
  N65: S15.2, D12.A
  N66: S16.2, D13.A
  N67: S17.2, D14.A
  N68: S18.2, D15.A
  N69: S19.2, D16.A
  N70: S20.2, D17.A
  N71: S21.2, D18.A
  N72: S22.2, D19.A
  N73: S23.2, D20.A
  N74: S24.2, D21.A
  N75: S25.2, D22.A
  N76: S26.2, D23.A
  N77: S27.2, D24.A
  N78: S28.2, D25.A
  N79: S29.2, D26.A
  N80: S30.2, D27.A
  N81: S31.2, D28.A
  N82: S32.2, D29.A
  N83: S33.2, D30.A
  N84: S34.2, D31.A
  N85: S35.2, D32.A
  N86: S36.2, D33.A
  N87: S37.2, D34.A
  N88: S38.2, D35.A
  N89: S39.2, D36.A
  N90: S40.2, D37.A
  N91: S41.2, D38.A
  N92: S42.2, D39.A
  N93: S43.2, D40.A
  N94: S44.2, D41.A
  N95: S45.2, D42.A
  N96: S46.2, D43.A
  N97: S47.2, D44.A
  N98: S48.2, D45.A
  N99: S50.2, D47.A
  N100: S51.2, D48.A
  N101: S52.2, D49.A
  N102: S53.2, D50.A
  N103: S54.2, D51.A
  N104: S55.2, D52.A
